# Fritzing sketch Diagram (saved by Fritzing 0.9.3b)

parts:
  PIR1 = PIR sensor
  Part1 = Arduino Uno (Rev3) - ICSP
  Photocell = mystery part, 4 pins [chip_label=?]
  KY-1 = Keyes Relay [package=THT]

nets:
  N1: PIR1.SIG, Part1.D3_PWM
  GND: PIR1.GND, Part1.GND, Photocell.pin1, KY-1.power
  N2: Part1.A0, Photocell.pin4
  N3: Part1.D2, KY-1.ground
  N4: Part1.5V, Photocell.pin3, KY-1.signal

notes:
  Photocell

custom parts:
  Keyes Relay: The Keyes 5V relay module is suitable for SCM development, home appliance control. It uses a 5V~12V TIL control signal which can control DC / AC signal.
